// Logisim project Q3.circ as structural Verilog: 1 circuit, main circuit main
module main (
  input  a2,
  input  a1,
  input  a0,
  output q
);

  wire and_1_out, and_2_out, and_3_out;

  and and_1 (and_1_out, a2, a1);
  and and_2 (and_2_out, a1, a0);
  and and_3 (and_3_out, a0, a2);
  or or_1 (q, and_1_out, and_2_out, and_3_out);
endmodule
