// Logisim project Q4.circ as structural Verilog: 1 circuit, main circuit main
module main (
  input  A,
  input  B,
  input  C,
  output Q
);

  wire and_1_out, nor_1_out;

  and and_1 (and_1_out, B, nor_1_out);
  nor nor_1 (nor_1_out, C, C);
  nor nor_2 (Q, A, and_1_out);
endmodule
